// Logisim project 3-voter.circ as structural Verilog: 1 circuit, main circuit main
module main (
  input  X,
  input  Y,
  input  Z,
  output F
);

  wire AND1_out, AND2_out, AND3_out;

  and AND1 (AND1_out, X, Y);
  and AND2 (AND2_out, Y, Z);
  and AND3 (AND3_out, X, Z);
  or OR (F, AND1_out, AND2_out, AND3_out);
endmodule
