// Logisim project 3-8-Decoder.circ as structural Verilog: 1 circuit, main circuit main
module main (
  input  G1,
  input  G2A_L,
  input  G2B_L,
  input  A,
  input  B,
  input  C,
  output Y0_L,
  output Y1_L,
  output Y2_L,
  output Y3_L,
  output Y4_L,
  output Y5_L,
  output Y6_L,
  output Y7_L
);

  wire and_1_out, not_1_out, not_2_out, not_3_out, not_4_out, not_5_out, not_6_out;

  and and_1 (and_1_out, G1, ~G2A_L, ~G2B_L);  // AND_Gate
  not not_1 (not_1_out, A);
  not not_2 (not_2_out, B);
  not not_3 (not_3_out, C);
  not not_4 (not_4_out, not_1_out);
  not not_5 (not_5_out, not_2_out);
  not not_6 (not_6_out, not_3_out);
  nand nand_1 (Y0_L, not_1_out, not_2_out, not_3_out, and_1_out);
  nand nand_2 (Y1_L, not_4_out, not_2_out, not_3_out, and_1_out);
  nand nand_3 (Y2_L, not_1_out, not_5_out, not_3_out, and_1_out);
  nand nand_4 (Y3_L, not_4_out, not_5_out, not_3_out, and_1_out);
  nand nand_5 (Y4_L, not_1_out, not_2_out, not_6_out, and_1_out);
  nand nand_6 (Y5_L, not_4_out, not_2_out, not_6_out, and_1_out);
  nand nand_7 (Y6_L, not_1_out, not_5_out, not_6_out, and_1_out);
  nand nand_8 (Y7_L, not_4_out, not_5_out, not_6_out, and_1_out);
endmodule
