// Logisim project 4 位二进制补码加法器溢出检测电路.circ as structural Verilog: 2 circuits, main circuit main
module main (
  input  A0,
  input  B0,
  input  A1,
  input  B1,
  input  A2,
  input  B2,
  input  A3,
  input  B3
);

  wire FA0_cout, FA1_cout, FA2_cout, FA3_f, xnor_1_out, xor_1_out;
  wire [0:0] and_1_out;

  FA FA0 (.A(A0), .B(B0), .Cin(1'b0), .Cout(FA0_cout));  // open: F
  FA FA1 (.A(A1), .B(B1), .Cin(FA0_cout), .Cout(FA1_cout));  // open: F
  FA FA2 (.A(A2), .B(B2), .Cin(FA1_cout), .Cout(FA2_cout));  // open: F
  FA FA3 (.A(A3), .B(B3), .Cin(FA2_cout), .F(FA3_f));  // open: Cout
  xnor xnor_1 (xnor_1_out, A3, B3);
  xor xor_1 (xor_1_out, FA3_f, B3);
  and and_1 (and_1_out[0], xnor_1_out, xor_1_out);
  Hex_Digit_Display hex_digit_display_1 (.value({3'b000, and_1_out[0]}));  // open: dp

  // Notes on the sheet:
  //   Cout
endmodule

module FA (
  input  A,
  input  B,
  input  Cin,
  output Cout,
  output F
);

  wire and_1_out, and_2_out, and_3_out;

  and and_1 (and_1_out, A, B);
  and and_2 (and_2_out, B, Cin);
  and and_3 (and_3_out, A, Cin);
  or or_1 (Cout, and_1_out, and_2_out, and_3_out);
  xor xor_1 (F, A, B, Cin);
endmodule
