// Logisim project 4-ADD.circ as structural Verilog: 2 circuits, main circuit main
module main (
  input  A0,
  input  B0,
  input  Cin,
  input  A1,
  input  B1,
  input  A2,
  input  B2,
  input  A3,
  input  B3,
  output Y0,
  output Y1,
  output Y2,
  output Y3
);

  wire FA0_cout, FA1_cout, FA2_cout;
  wire [0:0] FA3_cout;

  Hex_Digit_Display hex_digit_display_1 (.value({3'b000, Cin}));  // open: dp
  Hex_Digit_Display hex_digit_display_2 (.value({A3, A2, A1, A0}));  // open: dp
  Hex_Digit_Display hex_digit_display_3 (.value({B3, B2, B1, B0}));  // open: dp
  FA FA0 (.A(A0), .B(B0), .Cin(Cin), .Cout(FA0_cout), .F(Y0));
  FA FA1 (.A(A1), .B(B1), .Cin(FA0_cout), .Cout(FA1_cout), .F(Y1));
  FA FA2 (.A(A2), .B(B2), .Cin(FA1_cout), .Cout(FA2_cout), .F(Y2));
  FA FA3 (.A(A3), .B(B3), .Cin(FA2_cout), .Cout(FA3_cout[0]), .F(Y3));
  Hex_Digit_Display hex_digit_display_4 (.value({Y3, Y2, Y1, Y0}));  // open: dp
  Hex_Digit_Display hex_digit_display_5 (.value({3'b000, FA3_cout[0]}));  // open: dp

  // Notes on the sheet:
  //   Cin
  //   A
  //   B
  //   SUM
  //   Cout
endmodule

module FA (
  input  A,
  input  B,
  input  Cin,
  output Cout,
  output F
);

  wire and_1_out, and_2_out, and_3_out;

  and and_1 (and_1_out, A, B);
  and and_2 (and_2_out, B, Cin);
  and and_3 (and_3_out, A, Cin);
  or or_1 (Cout, and_1_out, and_2_out, and_3_out);
  xor xor_1 (F, A, B, Cin);
endmodule
