// Logisim project 8-3-Priority-Encoder.circ as structural Verilog: 1 circuit, main circuit main
module main (
  input  I0,
  input  I1,
  input  I2,
  input  I3,
  input  I4,
  input  I5,
  input  I6,
  input  I7,
  output Y2,
  output Y1,
  output Y0
);

  wire and_1_out, and_2_out, and_3_out, and_4_out, and_5_out, and_6_out, and_7_out;

  and and_1 (and_1_out, ~I0, I1);  // AND_Gate
  or O2 (Y2, and_5_out, and_6_out, and_4_out, and_7_out);
  and and_2 (and_2_out, ~I0, ~I1, I2);  // AND_Gate
  or O1 (Y1, and_6_out, and_2_out, and_3_out, and_7_out);
  and and_3 (and_3_out, ~I0, ~I1, ~I2, I3);  // AND_Gate
  and and_4 (and_4_out, ~I0, ~I1, ~I2, ~I3, I4);  // AND_Gate
  or O0 (Y0, and_1_out, and_3_out, and_5_out, and_7_out);
  and and_5 (and_5_out, ~I0, ~I1, ~I2, ~I3, ~I4, I5);  // AND_Gate
  and and_6 (and_6_out, ~I0, ~I1, ~I2, ~I3, ~I4, ~I5, I6);  // AND_Gate
  Hex_Digit_Display hex_digit_display_1 (.value({1'b0, Y2, Y1, Y0}));  // open: dp
  and and_7 (and_7_out, ~I0, ~I1, ~I2, ~I3, ~I4, ~I5, ~I6, I7);  // AND_Gate
endmodule
