// Logisim project ALU.circ as structural Verilog: 6 circuits, main circuit main
module main (
  input  A,
  input  B,
  input  S2,
  input  S1,
  input  S0,
  output F
);

  wire add_1_sum, and_1_out, not_1_out, not_2_out, or_1_out, sub_1_diff, xnor_1_out;

  ADD add_1 (.A(A), .B(B), .Sum(add_1_sum));  // open: Cout
  SUB sub_1 (.A(A), .B(B), .Diff(sub_1_diff));  // open: Negative
  and and_1 (and_1_out, A, B);
  or or_1 (or_1_out, A, B);
  xnor xnor_1 (xnor_1_out, A, B);
  not not_1 (not_1_out, A);
  not not_2 (not_2_out, B);
  _8_1MUX u_8_1mux_1 (
    .D0(sub_1_diff), .D1(add_1_sum), .D2(and_1_out), .D3(or_1_out), .D4(xnor_1_out), .D5(not_1_out), .D6(A),
    .D7(not_2_out), .S0(S0), .S1(S1), .S2(S2), .Y(F));
endmodule

module _8_1MUX (
  input  D0,
  input  D1,
  input  D2,
  input  D3,
  input  D4,
  input  D5,
  input  D6,
  input  D7,
  input  S0,
  input  S1,
  input  S2,
  output Y
);

  wire _4_1MUX_2_y, _4_1MUX_y;

  _4_1MUX _4_1MUX (.D0(D0), .D1(D1), .D2(D2), .D3(D3), .S0(S0), .S1(S1), .Y(_4_1MUX_y));
  _4_1MUX _4_1MUX_2 (.D0(D4), .D1(D5), .D2(D6), .D3(D7), .S0(S0), .S1(S1), .Y(_4_1MUX_2_y));
  _2_1MUX _2_1MUX (.D0(_4_1MUX_y), .D1(_4_1MUX_2_y), .X(S2), .Y(Y));
endmodule

module _4_1MUX (
  input  D0,
  input  D1,
  input  D2,
  input  D3,
  input  S0,
  input  S1,
  output Y
);

  wire n2_1mux_1_y, n2_1mux_2_y;

  _2_1MUX u_2_1mux_1 (.D0(D0), .D1(D1), .X(S0), .Y(n2_1mux_1_y));
  _2_1MUX u_2_1mux_2 (.D0(D2), .D1(D3), .X(S0), .Y(n2_1mux_2_y));
  _2_1MUX u_2_1mux_3 (.D0(n2_1mux_1_y), .D1(n2_1mux_2_y), .X(S1), .Y(Y));

  // Notes on the sheet:
  //   2-1MUX
  //   2-1MUX
  //   2-1MUX
endmodule

module _2_1MUX (
  input  D0,
  input  D1,
  input  X,
  output Y
);

  wire transistor_1_out;

  Transistor transistor_1 (.in(1'b1), .out(transistor_1_out), .gate(X));
  Transistor #(.\type ("n")) transistor_2 (.in(1'b0), .out(transistor_1_out), .gate(X));
  // Transmission_Gate transmission_1: pin names not known; wires that end beside it: D0, X, transistor_1_out, Y
  // Transmission_Gate transmission_2: pin names not known; wires that end beside it: D1, transistor_1_out, X, Y
endmodule

module ADD (
  input  A,
  input  B,
  output Sum,
  output Cout
);

  wire and_1_out, and_2_out;

  and and_1 (and_1_out, A, ~B);  // AND_Gate
  and and_2 (and_2_out, ~A, B);  // AND_Gate
  and and_3 (Cout, A, B);
  or or_1 (Sum, and_1_out, and_2_out);
endmodule

module SUB (
  input  A,
  input  B,
  output Diff,
  output Negative
);

  wire and_1_out, and_2_out;

  and and_1 (and_1_out, A, ~B);  // AND_Gate
  and and_2 (and_2_out, ~A, B);  // AND_Gate
  and and_3 (Negative, ~A, B);  // AND_Gate
  or or_1 (Diff, and_1_out, and_2_out);
endmodule
