// Logisim project NJUCS.circ as structural Verilog: 1 circuit, main circuit main
module main (
);

  wire [6:0] slider_1_out, slider_2_out, slider_3_out, slider_4_out, slider_5_out, slider_6_out,
       slider_7_out, slider_8_out, slider_9_out, slider_10_out, slider_11_out, slider_12_out, slider_13_out,
       slider_14_out, slider_15_out, slider_16_out, slider_17_out, slider_18_out, slider_19_out,
       slider_20_out, slider_21_out, slider_22_out, slider_23_out, slider_24_out, slider_25_out,
       slider_26_out, slider_27_out, slider_28_out, slider_29_out, slider_30_out;

  Slider #(.width(7), .value('h7f)) slider_1 (.out(slider_1_out));
  Slider #(.width(7), .value('h20)) slider_2 (.out(slider_2_out));
  Slider #(.width(7), .value('h10)) slider_3 (.out(slider_3_out));
  Slider #(.width(7), .value('h8)) slider_4 (.out(slider_4_out));
  Slider #(.width(7), .value('h4)) slider_5 (.out(slider_5_out));
  Slider #(.width(7), .value('h2)) slider_6 (.out(slider_6_out));
  Slider #(.width(7), .value('h7f)) slider_7 (.out(slider_7_out));
  Slider #(.width(7)) slider_8 (.out(slider_8_out));
  Slider #(.width(7), .value('h2)) slider_9 (.out(slider_9_out));
  Slider #(.width(7), .value('h1)) slider_10 (.out(slider_10_out));
  Slider #(.width(7), .value('h1)) slider_11 (.out(slider_11_out));
  Slider #(.width(7), .value('h7e)) slider_12 (.out(slider_12_out));
  Slider #(.width(7)) slider_13 (.out(slider_13_out));
  Slider #(.width(7), .value('h7e)) slider_14 (.out(slider_14_out));
  Slider #(.width(7), .value('h1)) slider_15 (.out(slider_15_out));
  DotMatrix dotmatrix_1 (
    .col0(slider_1_out), .col1(slider_2_out), .col2(slider_3_out), .col3(slider_4_out), .col4(slider_5_out));
  DotMatrix dotmatrix_2 (
    .col0(slider_6_out), .col1(slider_7_out), .col2(slider_8_out), .col3(slider_9_out), .col4(slider_10_out));
  DotMatrix dotmatrix_3 (
    .col0(slider_11_out), .col1(slider_12_out), .col2(slider_13_out), .col3(slider_14_out),
    .col4(slider_15_out));
  DotMatrix dotmatrix_4 (
    .col0(slider_30_out), .col1(slider_29_out), .col2(slider_28_out), .col3(slider_27_out),
    .col4(slider_26_out));
  DotMatrix dotmatrix_5 (
    .col0(slider_25_out), .col1(slider_24_out), .col2(slider_23_out), .col3(slider_22_out),
    .col4(slider_21_out));
  DotMatrix dotmatrix_6 (
    .col0(slider_20_out), .col1(slider_19_out), .col2(slider_18_out), .col3(slider_17_out),
    .col4(slider_16_out));
  Slider #(.width(7), .value('h26)) slider_16 (.out(slider_16_out));
  Slider #(.width(7), .value('h49)) slider_17 (.out(slider_17_out));
  Slider #(.width(7), .value('h49)) slider_18 (.out(slider_18_out));
  Slider #(.width(7), .value('h49)) slider_19 (.out(slider_19_out));
  Slider #(.width(7), .value('h32)) slider_20 (.out(slider_20_out));
  Slider #(.width(7), .value('h22)) slider_21 (.out(slider_21_out));
  Slider #(.width(7), .value('h41)) slider_22 (.out(slider_22_out));
  Slider #(.width(7), .value('h41)) slider_23 (.out(slider_23_out));
  Slider #(.width(7), .value('h41)) slider_24 (.out(slider_24_out));
  Slider #(.width(7), .value('h3e)) slider_25 (.out(slider_25_out));
  Slider #(.width(7)) slider_26 (.out(slider_26_out));
  Slider #(.width(7), .value('h7e)) slider_27 (.out(slider_27_out));
  Slider #(.width(7), .value('h1)) slider_28 (.out(slider_28_out));
  Slider #(.width(7), .value('h1)) slider_29 (.out(slider_29_out));
  Slider #(.width(7), .value('h1)) slider_30 (.out(slider_30_out));
endmodule
