// Logisim project 0号寄存器始终存储数值0.circ as structural Verilog: 1 circuit, main circuit main
module main (
  input  [4:0] RA,
  input  [4:0] RW,
  input  [31:0] busW,
  input  WE,
  input  CLK,
  input  [4:0] RB,
  output [31:0] busA,
  output [31:0] busB
);

  wire and_1_out, and_2_out, and_3_out, and_4_out, and_5_out, and_6_out, and_7_out, and_8_out, and_9_out,
       and_10_out, and_11_out, and_12_out, and_13_out, and_14_out, and_15_out, and_16_out, and_17_out,
       and_18_out, and_19_out, and_20_out, and_21_out, and_22_out, and_23_out, and_24_out, and_25_out,
       and_26_out, and_27_out, and_28_out, and_29_out, and_30_out, and_31_out, and_32_out, decoder_1_out0,
       decoder_1_out1, decoder_1_out2, decoder_1_out3, decoder_1_out4, decoder_1_out5, decoder_1_out6,
       decoder_1_out7, decoder_1_out8, decoder_1_out9, decoder_1_out10, decoder_1_out11, decoder_1_out12,
       decoder_1_out13, decoder_1_out14, decoder_1_out15, decoder_1_out16, decoder_1_out17, decoder_1_out18,
       decoder_1_out19, decoder_1_out20, decoder_1_out21, decoder_1_out22, decoder_1_out23, decoder_1_out24,
       decoder_1_out25, decoder_1_out26, decoder_1_out27, decoder_1_out28, decoder_1_out29, decoder_1_out30,
       decoder_1_out31;
  wire [31:0] register_1_q, register_2_q, register_3_q, register_4_q, register_5_q, register_6_q,
       register_7_q, register_8_q, register_9_q, register_10_q, register_11_q, register_12_q, register_13_q,
       register_14_q, register_15_q, register_16_q, register_17_q, register_18_q, register_19_q,
       register_20_q, register_21_q, register_22_q, register_23_q, register_24_q, register_25_q,
       register_26_q, register_27_q, register_28_q, register_29_q, register_30_q, register_31_q,
       register_32_q;

  Decoder #(.select(5), .enable("false")) decoder_1 (
    .out0(decoder_1_out0), .out1(decoder_1_out1), .out2(decoder_1_out2), .out3(decoder_1_out3),
    .out4(decoder_1_out4), .out5(decoder_1_out5), .out6(decoder_1_out6), .out7(decoder_1_out7),
    .out8(decoder_1_out8), .out9(decoder_1_out9), .out10(decoder_1_out10), .out11(decoder_1_out11),
    .out12(decoder_1_out12), .out13(decoder_1_out13), .out14(decoder_1_out14), .out15(decoder_1_out15),
    .out16(decoder_1_out16), .out17(decoder_1_out17), .out18(decoder_1_out18), .out19(decoder_1_out19),
    .out20(decoder_1_out20), .out21(decoder_1_out21), .out22(decoder_1_out22), .out23(decoder_1_out23),
    .out24(decoder_1_out24), .out25(decoder_1_out25), .out26(decoder_1_out26), .out27(decoder_1_out27),
    .out28(decoder_1_out28), .out29(decoder_1_out29), .out30(decoder_1_out30), .out31(decoder_1_out31),
    .sel(RW));
  and and_1 (and_1_out, decoder_1_out0, WE, CLK);
  and and_2 (and_2_out, decoder_1_out1, WE, CLK);
  and and_3 (and_3_out, decoder_1_out2, WE, CLK);
  and and_4 (and_4_out, decoder_1_out3, WE, CLK);
  and and_5 (and_5_out, decoder_1_out4, WE, CLK);
  and and_6 (and_6_out, decoder_1_out5, WE, CLK);
  and and_7 (and_7_out, decoder_1_out6, WE, CLK);
  and and_8 (and_8_out, decoder_1_out7, WE, CLK);
  and and_9 (and_9_out, decoder_1_out8, WE, CLK);
  and and_10 (and_10_out, decoder_1_out9, WE, CLK);
  and and_11 (and_11_out, decoder_1_out10, WE, CLK);
  and and_12 (and_12_out, decoder_1_out11, WE, CLK);
  and and_13 (and_13_out, decoder_1_out12, WE, CLK);
  and and_14 (and_14_out, decoder_1_out13, WE, CLK);
  and and_15 (and_15_out, decoder_1_out14, WE, CLK);
  and and_16 (and_16_out, decoder_1_out15, WE, CLK);
  and and_17 (and_17_out, decoder_1_out16, WE, CLK);
  and and_18 (and_18_out, decoder_1_out17, WE, CLK);
  and and_19 (and_19_out, decoder_1_out18, WE, CLK);
  and and_20 (and_20_out, decoder_1_out19, WE, CLK);
  and and_21 (and_21_out, decoder_1_out20, WE, CLK);
  and and_22 (and_22_out, decoder_1_out21, WE, CLK);
  and and_23 (and_23_out, decoder_1_out22, WE, CLK);
  and and_24 (and_24_out, decoder_1_out23, WE, CLK);
  and and_25 (and_25_out, decoder_1_out24, WE, CLK);
  and and_26 (and_26_out, decoder_1_out25, WE, CLK);
  and and_27 (and_27_out, decoder_1_out26, WE, CLK);
  and and_28 (and_28_out, decoder_1_out27, WE, CLK);
  and and_29 (and_29_out, decoder_1_out28, WE, CLK);
  and and_30 (and_30_out, decoder_1_out29, WE, CLK);
  and and_31 (and_31_out, decoder_1_out30, WE, CLK);
  and and_32 (and_32_out, decoder_1_out31, WE, CLK);
  Register #(.width(32), .Select("low")) register_1 (
    .D({32{1'b0}}), .Q(register_1_q), .clk(and_1_out));  // open: en, clr
  Register #(.width(32), .Select("low")) register_2 (.D(busW), .Q(register_2_q), .clk(and_2_out));  // open: en, clr
  Register #(.width(32), .Select("low")) register_3 (.D(busW), .Q(register_3_q), .clk(and_3_out));  // open: en, clr
  Register #(.width(32), .Select("low")) register_4 (.D(busW), .Q(register_4_q), .clk(and_4_out));  // open: en, clr
  Register #(.width(32), .Select("low")) register_5 (.D(busW), .Q(register_5_q), .clk(and_5_out));  // open: en, clr
  Register #(.width(32), .Select("low")) register_6 (.D(busW), .Q(register_6_q), .clk(and_6_out));  // open: en, clr
  Register #(.width(32), .Select("low")) register_7 (.D(busW), .Q(register_7_q), .clk(and_7_out));  // open: en, clr
  Register #(.width(32), .Select("low")) register_8 (.D(busW), .Q(register_8_q), .clk(and_8_out));  // open: en, clr
  Register #(.width(32), .Select("low")) register_9 (.D(busW), .Q(register_9_q), .clk(and_9_out));  // open: en, clr
  Register #(.width(32), .Select("low")) register_10 (.D(busW), .Q(register_10_q), .clk(and_10_out));  // open: en, clr
  Register #(.width(32), .Select("low")) register_11 (.D(busW), .Q(register_11_q), .clk(and_11_out));  // open: en, clr
  Register #(.width(32), .Select("low")) register_12 (.D(busW), .Q(register_12_q), .clk(and_12_out));  // open: en, clr
  Register #(.width(32), .Select("low")) register_13 (.D(busW), .Q(register_13_q), .clk(and_13_out));  // open: en, clr
  Register #(.width(32), .Select("low")) register_14 (.D(busW), .Q(register_14_q), .clk(and_14_out));  // open: en, clr
  Register #(.width(32), .Select("low")) register_15 (.D(busW), .Q(register_15_q), .clk(and_15_out));  // open: en, clr
  Register #(.width(32), .Select("low")) register_16 (.D(busW), .Q(register_16_q), .clk(and_16_out));  // open: en, clr
  Register #(.width(32), .Select("low")) register_17 (.D(busW), .Q(register_17_q), .clk(and_17_out));  // open: en, clr
  Register #(.width(32), .Select("low")) register_18 (.D(busW), .Q(register_18_q), .clk(and_18_out));  // open: en, clr
  Register #(.width(32), .Select("low")) register_19 (.D(busW), .Q(register_19_q), .clk(and_19_out));  // open: en, clr
  Register #(.width(32), .Select("low")) register_20 (.D(busW), .Q(register_20_q), .clk(and_20_out));  // open: en, clr
  Register #(.width(32), .Select("low")) register_21 (.D(busW), .Q(register_21_q), .clk(and_21_out));  // open: en, clr
  Register #(.width(32), .Select("low")) register_22 (.D(busW), .Q(register_22_q), .clk(and_22_out));  // open: en, clr
  Register #(.width(32), .Select("low")) register_23 (.D(busW), .Q(register_23_q), .clk(and_23_out));  // open: en, clr
  Register #(.width(32), .Select("low")) register_24 (.D(busW), .Q(register_24_q), .clk(and_24_out));  // open: en, clr
  Register #(.width(32), .Select("low")) register_25 (.D(busW), .Q(register_25_q), .clk(and_25_out));  // open: en, clr
  Register #(.width(32), .Select("low")) register_26 (.D(busW), .Q(register_26_q), .clk(and_26_out));  // open: en, clr
  Register #(.width(32), .Select("low")) register_27 (.D(busW), .Q(register_27_q), .clk(and_27_out));  // open: en, clr
  Register #(.width(32), .Select("low")) register_28 (.D(busW), .Q(register_28_q), .clk(and_28_out));  // open: en, clr
  Register #(.width(32), .Select("low")) register_29 (.D(busW), .Q(register_29_q), .clk(and_29_out));  // open: en, clr
  Register #(.width(32), .Select("low")) register_30 (.D(busW), .Q(register_30_q), .clk(and_30_out));  // open: en, clr
  Register #(.width(32), .Select("low")) register_31 (.D(busW), .Q(register_31_q), .clk(and_31_out));  // open: en, clr
  Register #(.width(32), .Select("low")) register_32 (.D(busW), .Q(register_32_q), .clk(and_32_out));  // open: en, clr
  Multiplexer #(.select(5), .width(32), .enable("false")) multiplexer_1 (
    .in0(register_1_q), .in1(register_2_q), .in2(register_3_q), .in3(register_4_q), .in4(register_5_q),
    .in5(register_6_q), .in6(register_7_q), .in7(register_8_q), .in8(register_9_q), .in9(register_10_q),
    .in10(register_11_q), .in11(register_12_q), .in12(register_13_q), .in13(register_14_q),
    .in14(register_15_q), .in15(register_16_q), .in16(register_17_q), .in17(register_18_q),
    .in18(register_19_q), .in19(register_20_q), .in20(register_21_q), .in21(register_22_q),
    .in22(register_23_q), .in23(register_24_q), .in24(register_25_q), .in25(register_26_q),
    .in26(register_27_q), .in27(register_28_q), .in28(register_29_q), .in29(register_30_q),
    .in30(register_31_q), .in31(register_32_q), .out(busA), .sel(RA));
  Multiplexer #(.select(5), .width(32), .enable("false")) multiplexer_2 (
    .in0(register_1_q), .in1(register_2_q), .in2(register_3_q), .in3(register_4_q), .in4(register_5_q),
    .in5(register_6_q), .in6(register_7_q), .in7(register_8_q), .in8(register_9_q), .in9(register_10_q),
    .in10(register_11_q), .in11(register_12_q), .in12(register_13_q), .in13(register_14_q),
    .in14(register_15_q), .in15(register_16_q), .in16(register_17_q), .in17(register_18_q),
    .in18(register_19_q), .in19(register_20_q), .in20(register_21_q), .in21(register_22_q),
    .in22(register_23_q), .in23(register_24_q), .in24(register_25_q), .in25(register_26_q),
    .in26(register_27_q), .in27(register_28_q), .in28(register_29_q), .in29(register_30_q),
    .in30(register_31_q), .in31(register_32_q), .out(busB), .sel(RB));
endmodule
