// Logisim project 任意初始值开始的10进制计数器.circ as structural Verilog: 4 circuits, main circuit main
module main (
  input  LD,
  input  Clr,
  input  A0,
  input  A1,
  input  A2,
  input  A3,
  output Y0,
  output Y1,
  output Y2,
  output Y3
);

  wire and_1_out, clock_1_out, \n4位加法器_1_y0 , \n4位加法器_1_y1 , \n4位加法器_1_y2 , \n4位加法器_1_y3 , or_1_out,
       xnor_1_out, xnor_2_out, xnor_3_out, xnor_4_out;

  or or_1 (or_1_out, LD, and_1_out);
  Clock clock_1 (.out(clock_1_out));
  CNTR4U cntr4u_1 (
    .Clk(clock_1_out), .LD(or_1_out), .Clr(Clr), .D0(A0), .D1(A1), .D2(A2), .D3(A3), .ENP(1'b1), .ENT(1'b1),
    .Q0(Y0), .Q1(Y1), .Q2(Y2), .Q3(Y3));  // open: RCO
  \_4位加法器  \u_4位加法器_1  (
    .A0(A0), .B0(1'b1), .Cin(1'b0), .A1(A1), .B1(1'b0), .A2(A2), .B2(1'b0), .A3(A3), .B3(1'b1),
    .Y0(\n4位加法器_1_y0 ), .Y1(\n4位加法器_1_y1 ), .Y2(\n4位加法器_1_y2 ), .Y3(\n4位加法器_1_y3 ));
  xnor xnor_1 (xnor_1_out, Y0, \n4位加法器_1_y0 );
  xnor xnor_2 (xnor_2_out, Y1, \n4位加法器_1_y1 );
  xnor xnor_3 (xnor_3_out, Y2, \n4位加法器_1_y2 );
  xnor xnor_4 (xnor_4_out, Y3, \n4位加法器_1_y3 );
  Hex_Digit_Display hex_digit_display_1 (.value({Y3, Y2, Y1, Y0}));  // open: dp
  and and_1 (and_1_out, xnor_1_out, xnor_2_out, xnor_3_out, xnor_4_out);
endmodule

module CNTR4U (
  input  Clk,
  input  LD,
  input  Clr,
  input  D0,
  input  D1,
  input  D2,
  input  D3,
  input  ENP,
  input  ENT,
  output Q0,
  output Q1,
  output Q2,
  output Q3,
  output RCO
);

  wire and_1_out, and_2_out, and_3_out, and_4_out, and_5_out, and_6_out, and_7_out, and_8_out, and_10_out,
       and_11_out, and_12_out, and_13_out, and_14_out, and_15_out, and_16_out, and_17_out, buffer_1_out,
       d_ff_1_qn, d_ff_2_qn, d_ff_3_qn, d_ff_4_qn, not_1_out, not_2_out, or_1_out, or_2_out, or_3_out,
       or_4_out, xor_1_out, xor_2_out, xor_3_out, xor_4_out;

  buf buffer_1 (buffer_1_out, Clr);
  not not_1 (not_1_out, d_ff_1_qn);
  and and_1 (and_1_out, ~d_ff_2_qn, ~d_ff_1_qn);  // AND_Gate
  and and_2 (and_2_out, ~d_ff_3_qn, ~d_ff_2_qn, ~d_ff_1_qn);  // AND_Gate
  and and_3 (and_3_out, ENP, ENT);
  and and_4 (and_4_out, not_1_out, and_3_out);
  and and_5 (and_5_out, and_1_out, and_3_out);
  and and_6 (and_6_out, and_2_out, and_3_out);
  not not_2 (not_2_out, ENT);
  and and_7 (and_7_out, LD, ~buffer_1_out);  // AND_Gate
  and and_8 (and_8_out, ~and_7_out, ~buffer_1_out);  // AND_Gate
  xor xor_1 (xor_1_out, and_3_out, ~d_ff_1_qn);  // XOR_Gate
  xor xor_2 (xor_2_out, and_4_out, ~d_ff_2_qn);  // XOR_Gate
  xor xor_3 (xor_3_out, and_5_out, ~d_ff_3_qn);  // XOR_Gate
  xor xor_4 (xor_4_out, and_6_out, ~d_ff_4_qn);  // XOR_Gate
  and and_9 (RCO, ~d_ff_4_qn, ~d_ff_3_qn, ~d_ff_2_qn, ~d_ff_1_qn, ~not_2_out);  // AND_Gate
  and and_10 (and_10_out, and_7_out, D0);
  and and_11 (and_11_out, and_8_out, xor_1_out);
  and and_12 (and_12_out, and_7_out, D1);
  and and_13 (and_13_out, and_8_out, xor_2_out);
  and and_14 (and_14_out, and_7_out, D2);
  and and_15 (and_15_out, and_8_out, xor_3_out);
  and and_16 (and_16_out, and_7_out, D3);
  and and_17 (and_17_out, and_8_out, xor_4_out);
  or or_1 (or_1_out, and_10_out, and_11_out);
  or or_2 (or_2_out, and_12_out, and_13_out);
  or or_3 (or_3_out, and_14_out, and_15_out);
  or or_4 (or_4_out, and_16_out, and_17_out);
  D_Flip_Flop d_ff_1 (.clk(Clk), .D(or_1_out), .Q(Q0), .Qn(d_ff_1_qn));  // open: preset, reset
  D_Flip_Flop d_ff_2 (.clk(Clk), .D(or_2_out), .Q(Q1), .Qn(d_ff_2_qn));  // open: preset, reset
  D_Flip_Flop d_ff_3 (.clk(Clk), .D(or_3_out), .Q(Q2), .Qn(d_ff_3_qn));  // open: preset, reset
  D_Flip_Flop d_ff_4 (.clk(Clk), .D(or_4_out), .Q(Q3), .Qn(d_ff_4_qn));  // open: preset, reset
  LED led_1 (.in(RCO));
endmodule

// ADD
module \_4位加法器  (
  input  A0,
  input  B0,
  input  Cin,
  input  A1,
  input  B1,
  input  A2,
  input  B2,
  input  A3,
  input  B3,
  output Y0,
  output Y1,
  output Y2,
  output Y3
);

  wire FA0_cout, FA1_cout, FA2_cout;
  wire [0:0] FA3_cout;

  Hex_Digit_Display hex_digit_display_1 (.value({3'b000, Cin}));  // open: dp
  Hex_Digit_Display hex_digit_display_2 (.value({A3, A2, A1, A0}));  // open: dp
  Hex_Digit_Display hex_digit_display_3 (.value({B3, B2, B1, B0}));  // open: dp
  FA FA0 (.A(A0), .B(B0), .Cin(Cin), .Cout(FA0_cout), .F(Y0));
  FA FA1 (.A(A1), .B(B1), .Cin(FA0_cout), .Cout(FA1_cout), .F(Y1));
  FA FA2 (.A(A2), .B(B2), .Cin(FA1_cout), .Cout(FA2_cout), .F(Y2));
  FA FA3 (.A(A3), .B(B3), .Cin(FA2_cout), .Cout(FA3_cout[0]), .F(Y3));
  Hex_Digit_Display hex_digit_display_4 (.value({Y3, Y2, Y1, Y0}));  // open: dp
  Hex_Digit_Display hex_digit_display_5 (.value({3'b000, FA3_cout[0]}));  // open: dp

  // Notes on the sheet:
  //   Cin
  //   A
  //   B
  //   SUM
  //   Cout
endmodule

module FA (
  input  A,
  input  B,
  input  Cin,
  output Cout,
  output F
);

  wire and_1_out, and_2_out, and_3_out;

  and and_1 (and_1_out, A, B);
  and and_2 (and_2_out, B, Cin);
  and and_3 (and_3_out, A, Cin);
  or or_1 (Cout, and_1_out, and_2_out, and_3_out);
  xor xor_1 (F, A, B, Cin);
endmodule
