// Logisim project 重复生成二进制序列.circ as structural Verilog: 3 circuits, main circuit main
module main (
  input  Clear,
  input  Clr,
  input  S1,
  input  S0,
  output QA,
  output QB,
  output QC,
  output QD
);

  wire clock_1_out, \反馈电路_1_y ;

  Clock clock_1 (.out(clock_1_out));
  \_4位通用移位寄存器  \u_4位通用移位寄存器_1  (
    .Clk(clock_1_out), .Clr(Clr), .LIN(\反馈电路_1_y ), .D(1'b1), .C(1'b0), .B(1'b0), .S1(S1), .S0(S0), .A(1'b0),
    .RIN(1'b0), .QD(QD), .QC(QC), .QB(QB), .QA(QA));
  // Digital_Oscilloscope #(.nState(18)) digital_oscilloscope_1: pin names not known; wires that end beside it: clock_1_out, QA, QB, Clear
  \反馈电路  \u_反馈电路_1  (.QD(QD), .QC(QC), .QB(QB), .QA(QA), .Y(\反馈电路_1_y ));
  Hex_Digit_Display hex_digit_display_1 (.value({QA, QB, QC, QD}));  // open: dp
endmodule

module \_4位通用移位寄存器  (
  input  Clk,
  input  Clr,
  input  LIN,
  input  D,
  input  C,
  input  B,
  input  S1,
  input  S0,
  input  A,
  input  RIN,
  output QD,
  output QC,
  output QB,
  output QA
);

  wire and_1_out, and_2_out, and_3_out, and_4_out, and_5_out, and_6_out, and_7_out, and_8_out, and_9_out,
       and_10_out, and_11_out, and_12_out, and_13_out, and_14_out, and_15_out, and_16_out, not_1_out,
       not_2_out, not_3_out, not_4_out, not_5_out, or_1_out, or_2_out, or_3_out, or_4_out;

  not not_1 (not_1_out, S1);
  not not_2 (not_2_out, S0);
  not not_3 (not_3_out, Clr);
  not not_4 (not_4_out, not_1_out);
  not not_5 (not_5_out, not_2_out);
  and and_1 (and_1_out, not_3_out, LIN, not_4_out, not_2_out);
  and and_2 (and_2_out, not_3_out, QD, not_1_out, not_2_out);
  and and_3 (and_3_out, not_3_out, D, not_4_out, not_5_out);
  and and_4 (and_4_out, not_3_out, QC, not_1_out, not_5_out);
  and and_5 (and_5_out, not_3_out, QD, not_4_out, not_2_out);
  and and_6 (and_6_out, not_3_out, QC, not_1_out, not_2_out);
  and and_7 (and_7_out, not_3_out, C, not_4_out, not_5_out);
  and and_8 (and_8_out, not_3_out, QB, not_1_out, not_5_out);
  and and_9 (and_9_out, not_3_out, QC, not_4_out, not_2_out);
  and and_10 (and_10_out, not_3_out, QB, not_1_out, not_2_out);
  and and_11 (and_11_out, not_3_out, B, not_4_out, not_5_out);
  and and_12 (and_12_out, not_3_out, QA, not_1_out, not_5_out);
  and and_13 (and_13_out, not_3_out, QB, not_4_out, not_2_out);
  and and_14 (and_14_out, not_3_out, QA, not_1_out, not_2_out);
  and and_15 (and_15_out, not_3_out, A, not_4_out, not_5_out);
  and and_16 (and_16_out, not_3_out, RIN, not_1_out, not_5_out);
  or or_1 (or_1_out, and_1_out, and_2_out, and_3_out, and_4_out);
  or or_2 (or_2_out, and_5_out, and_6_out, and_7_out, and_8_out);
  or or_3 (or_3_out, and_9_out, and_10_out, and_11_out, and_12_out);
  or or_4 (or_4_out, and_13_out, and_14_out, and_15_out, and_16_out);
  D_Flip_Flop d_ff_1 (.clk(Clk), .D(or_1_out), .Q(QD));  // open: Qn, preset, reset
  D_Flip_Flop d_ff_2 (.clk(Clk), .D(or_2_out), .Q(QC));  // open: Qn, preset, reset
  D_Flip_Flop d_ff_3 (.clk(Clk), .D(or_3_out), .Q(QB));  // open: Qn, preset, reset
  D_Flip_Flop d_ff_4 (.clk(Clk), .D(or_4_out), .Q(QA));  // open: Qn, preset, reset
endmodule

module \反馈电路  (
  input  QD,
  input  QC,
  input  QB,
  input  QA,
  output Y
);

  wire and_1_out, and_2_out;

  and and_1 (and_1_out, QA, ~QB);  // AND_Gate
  and and_2 (and_2_out, QB, ~QA);  // AND_Gate
  or or_1 (Y, and_1_out, and_2_out);
endmodule
