// Logisim project （一种遇到的典型困难）组合电路实现4位移位寄存器.circ as structural Verilog: 1 circuit, main circuit main
module main (
  input  Din,
  output Y3,
  output Y2,
  output Y1,
  output Y0
);

  wire [3:0] adder_1_out, bit_extender_1_out, multiplexer_1_out, shifter_1_out;

  Multiplexer #(.select(4), .width(4), .enable("false")) multiplexer_1 (
    .in0(4'b0000), .in1(4'b0001), .in2(4'b0010), .in3(4'b0011), .in4(4'b0100), .in5(4'b0101), .in6(4'b0110),
    .in7(4'b0111), .in8(4'b1000), .in9(4'b1001), .in10(4'b1010), .in11(4'b1011), .in12(4'b1100),
    .in13(4'b1101), .in14(4'b1110), .in15(4'b1111), .out(multiplexer_1_out), .sel(adder_1_out));
  BitSelector #(.width(4)) bitselector_1 (.in(multiplexer_1_out), .out(Y0), .sel(2'b00));
  BitSelector #(.width(4)) bitselector_2 (.in(multiplexer_1_out), .out(Y1), .sel(2'b01));
  BitSelector #(.width(4)) bitselector_3 (.in(multiplexer_1_out), .out(Y2), .sel(2'b10));
  BitSelector #(.width(4)) bitselector_4 (.in(multiplexer_1_out), .out(Y3), .sel(2'b11));
  Shifter #(.width(4)) shifter_1 (.in(multiplexer_1_out), .\dist (2'b01), .out(shifter_1_out));
  assign bit_extender_1_out = {{3{1'b0}}, Din};  // Bit_Extender bit_extender_1
  Adder #(.width(4)) adder_1 (.a(shifter_1_out), .b(bit_extender_1_out), .out(adder_1_out));  // open: cin, cout
endmodule
