// Logisim project 32位算术逻辑运算单元ALU.circ as structural Verilog: 9 circuits, main circuit main
module main (
  input  [31:0] A,
  input  [31:0] B,
  input  [3:0] ALUctr,
  output Zero,
  output [31:0] Result
);

  wire \alu操作控制信号生成部件_1_sigctr , \alu操作控制信号生成部件_1_subctr , multiplexer_2_out, \n32位快速加法器_1_cf ,
       \n32位快速加法器_1_of , \n32位快速加法器_1_sf , xnor_1_out, xor_1_out;
  wire [1:0] \alu操作控制信号生成部件_1_opctr ;
  wire [31:0] bit_extender_1_out, bit_extender_2_out, \n32位快速加法器_1_f , \异或门阵列_1_cout , \或门阵列_1_cout ;

  // Probe on A
  // Probe on B
  // Probe on A
  assign bit_extender_1_out = {{31{\alu操作控制信号生成部件_1_subctr }}, \alu操作控制信号生成部件_1_subctr };  // Bit_Extender bit_extender_1
  \异或门阵列  \u_异或门阵列_1  (.A(B), .B(bit_extender_1_out), .Cout(\异或门阵列_1_cout ));
  \或门阵列  \u_或门阵列_1  (.A(A), .B(B), .Cout(\或门阵列_1_cout ));
  // Probe on B
  \_32位快速加法器  \u_32位快速加法器_1  (
    .C0(\alu操作控制信号生成部件_1_subctr ), .A(A), .B(\异或门阵列_1_cout ), .ZF(Zero), .CF(\n32位快速加法器_1_cf ),
    .F(\n32位快速加法器_1_f ), .OF(\n32位快速加法器_1_of ), .SF(\n32位快速加法器_1_sf ));
  xnor xnor_1 (xnor_1_out, \alu操作控制信号生成部件_1_subctr , \n32位快速加法器_1_cf );
  xor xor_1 (xor_1_out, \n32位快速加法器_1_of , \n32位快速加法器_1_sf );
  Multiplexer #(.select(2), .width(32), .enable("false")) multiplexer_1 (
    .in0(\n32位快速加法器_1_f ), .in1(\或门阵列_1_cout ), .in2(B), .in3(bit_extender_2_out), .out(Result),
    .sel(\alu操作控制信号生成部件_1_opctr ));
  \ALU操作控制信号生成部件  \alu操作控制信号生成部件_1  (
    .ALUctr(ALUctr), .SUBctr(\alu操作控制信号生成部件_1_subctr ), .OPctr(\alu操作控制信号生成部件_1_opctr ),
    .SIGctr(\alu操作控制信号生成部件_1_sigctr ));
  Multiplexer #(.enable("false")) multiplexer_2 (
    .in0(xnor_1_out), .in1(xor_1_out), .out(multiplexer_2_out), .sel(\alu操作控制信号生成部件_1_sigctr ));
  assign bit_extender_2_out = {{31{1'b0}}, multiplexer_2_out};  // Bit_Extender bit_extender_2
  // Probe on Result

  // Notes on the sheet:
  //   SUBctr
  //   OPctr
  //   SIGctr
endmodule

// CLA
module \_4位CLA  (
  input  B3,
  input  A3,
  input  B2,
  input  A2,
  input  B1,
  input  A1,
  input  B0,
  input  A0,
  input  C0,
  output C4,
  output S3,
  output C3,
  output [3:0] S,
  output S2,
  output S1,
  output S0,
  output Gg,
  output Pg
);

  wire and_1_out, and_2_out, and_3_out, and_4_out, and_6_out, and_7_out, nand_1_out, nand_2_out, nand_3_out,
       nand_4_out, nor_1_out, nor_2_out, nor_3_out, nor_4_out, not_1_out, not_2_out, not_3_out, not_4_out,
       not_5_out, not_6_out, or_1_out, or_2_out, or_3_out, or_4_out, or_5_out, or_6_out, or_7_out, or_8_out,
       or_9_out, or_10_out;

  nand nand_1 (nand_1_out, B3, A3);
  nor nor_1 (nor_1_out, B3, A3);
  nand nand_2 (nand_2_out, B2, A2);
  nor nor_2 (nor_2_out, B2, A2);
  nand nand_3 (nand_3_out, B1, A1);
  nor nor_3 (nor_3_out, B1, A1);
  nand nand_4 (nand_4_out, B0, A0);
  nor nor_4 (nor_4_out, B0, A0);
  not not_1 (not_1_out, C0);
  not not_2 (not_2_out, nor_1_out);
  or or_1 (or_1_out, ~nor_2_out, ~nand_1_out);  // OR_Gate
  or or_2 (or_2_out, ~nor_3_out, ~nand_1_out, ~nand_2_out);  // OR_Gate
  or or_3 (or_3_out, ~nor_4_out, ~nand_1_out, ~nand_2_out, ~nand_3_out);  // OR_Gate
  or or_4 (or_4_out, ~nand_1_out, ~nand_2_out, ~nand_3_out, ~nand_4_out, ~not_1_out);  // OR_Gate
  and and_1 (and_1_out, nand_1_out, ~nor_1_out);  // AND_Gate
  not not_3 (not_3_out, nor_2_out);
  or or_5 (or_5_out, ~nor_3_out, ~nand_2_out);  // OR_Gate
  or or_6 (or_6_out, ~nor_4_out, ~nand_2_out, ~nand_3_out);  // OR_Gate
  or or_7 (or_7_out, ~nand_2_out, ~nand_3_out, ~nand_4_out, ~not_1_out);  // OR_Gate
  and and_2 (and_2_out, nand_2_out, ~nor_2_out);  // AND_Gate
  not not_4 (not_4_out, nor_3_out);
  or or_8 (or_8_out, ~nand_3_out, ~nor_4_out);  // OR_Gate
  or or_9 (or_9_out, ~nand_3_out, ~nand_4_out, ~not_1_out);  // OR_Gate
  and and_3 (and_3_out, nand_3_out, ~nor_3_out);  // AND_Gate
  not not_5 (not_5_out, nor_4_out);
  or or_10 (or_10_out, ~nand_4_out, ~not_1_out);  // OR_Gate
  and and_4 (and_4_out, nand_4_out, ~nor_4_out);  // AND_Gate
  not not_6 (not_6_out, not_1_out);
  Gg_Pg gg_pg_1 (.A0(A0), .A1(A1), .A2(A2), .A3(A3), .B0(B0), .B1(B1), .B2(B2), .B3(B3), .Gg(Gg), .Pg(Pg));
  and and_5 (C3, not_3_out, or_5_out, or_6_out, or_7_out);
  and and_6 (and_6_out, not_4_out, or_8_out, or_9_out);
  and and_7 (and_7_out, not_5_out, or_10_out);
  and and_8 (C4, not_2_out, or_1_out, or_2_out, or_3_out, or_4_out);
  xor xor_1 (S[3], and_1_out, C3);
  xor xor_2 (S[2], and_2_out, and_6_out);
  xor xor_3 (S[1], and_3_out, and_7_out);
  xor xor_4 (S[0], and_4_out, not_6_out);

  assign S0 = S[0];
  assign S1 = S[1];
  assign S2 = S[2];
  assign S3 = S[3];
endmodule

// CLU
module \_4位CLU  (
  input  C0,
  input  P0,
  input  G0,
  input  P1,
  input  G1,
  input  P2,
  input  G2,
  input  P3,
  input  G3,
  output C1,
  output C2,
  output C3,
  output C4
);

  wire and_1_out, and_2_out, and_3_out, and_4_out, and_5_out, and_6_out, and_7_out, and_8_out, and_9_out,
       and_10_out;

  or or_1 (C1, and_1_out, G0);
  and and_1 (and_1_out, C0, P0);
  or or_2 (C2, and_2_out, and_3_out, G1);
  and and_2 (and_2_out, C0, P0, P1);
  and and_3 (and_3_out, G0, P1);
  and and_4 (and_4_out, G0, P1, P2);
  and and_5 (and_5_out, C0, P0, P1, P2);
  or or_3 (C3, and_5_out, and_4_out, and_6_out, G2);
  and and_6 (and_6_out, G1, P2);
  and and_7 (and_7_out, C0, P0, P1, P2, P3);
  and and_8 (and_8_out, G0, P1, P2, P3);
  or or_4 (C4, and_7_out, and_8_out, and_9_out, and_10_out, G3);
  and and_9 (and_9_out, G1, P2, P3);
  and and_10 (and_10_out, G2, P3);
endmodule

module \_16位先行进位加法器  (
  input  C0,
  input  [15:0] A,
  input  [15:0] B,
  output [15:0] S,
  output C16,
  output C15,
  output F_n_1
);

  wire \n4位cla_1_gg , \n4位cla_1_pg , \n4位cla_2_gg , \n4位cla_2_pg , \n4位cla_3_gg , \n4位cla_3_pg ,
       \n4位cla_4_gg , \n4位cla_4_pg , \n4位clu_1_c1 , \n4位clu_1_c2 , \n4位clu_1_c3 ;

  // Probe on A
  // Probe on B
  \_4位CLA  \u_4位cla_1  (
    .B3(B[3]), .A3(A[3]), .B2(B[2]), .A2(A[2]), .B1(B[1]), .A1(A[1]), .B0(B[0]), .A0(A[0]), .C0(C0),
    .S(S[3:0]), .Gg(\n4位cla_1_gg ), .Pg(\n4位cla_1_pg ));  // open: C4, S3, C3, S2, S1, S0
  \_4位CLA  \u_4位cla_2  (
    .B3(B[7]), .A3(A[7]), .B2(B[6]), .A2(A[6]), .B1(B[5]), .A1(A[5]), .B0(B[4]), .A0(A[4]),
    .C0(\n4位clu_1_c1 ), .S(S[7:4]), .Gg(\n4位cla_2_gg ), .Pg(\n4位cla_2_pg ));  // open: C4, S3, C3, S2, S1, S0
  \_4位CLA  \u_4位cla_3  (
    .B3(B[11]), .A3(A[11]), .B2(B[10]), .A2(A[10]), .B1(B[9]), .A1(A[9]), .B0(B[8]), .A0(A[8]),
    .C0(\n4位clu_1_c2 ), .S(S[11:8]), .Gg(\n4位cla_3_gg ), .Pg(\n4位cla_3_pg ));  // open: C4, S3, C3, S2, S1, S0
  \_4位CLA  \u_4位cla_4  (
    .B3(B[15]), .A3(A[15]), .B2(B[14]), .A2(A[14]), .B1(B[13]), .A1(A[13]), .B0(B[12]), .A0(A[12]),
    .C0(\n4位clu_1_c3 ), .C4(C16), .S3(F_n_1), .C3(C15), .S(S[15:12]), .Gg(\n4位cla_4_gg ), .Pg(\n4位cla_4_pg ));  // open: S2, S1, S0
  \_4位CLU  \u_4位clu_1  (
    .C0(C0), .C1(\n4位clu_1_c1 ), .C2(\n4位clu_1_c2 ), .C3(\n4位clu_1_c3 ), .P0(\n4位cla_1_pg ),
    .G0(\n4位cla_1_gg ), .P1(\n4位cla_2_pg ), .G1(\n4位cla_2_gg ), .P2(\n4位cla_3_pg ), .G2(\n4位cla_3_gg ),
    .P3(\n4位cla_4_pg ), .G3(\n4位cla_4_gg ));  // open: C4
  // Probe on S
endmodule

module Gg_Pg (
  input  A0,
  input  A1,
  input  A2,
  input  A3,
  input  B0,
  input  B1,
  input  B2,
  input  B3,
  output Gg,
  output Pg
);

  wire and_1_out, and_2_out, and_3_out, and_4_out, and_5_out, and_6_out, and_7_out, or_1_out, or_2_out,
       or_3_out, or_4_out;

  or or_1 (or_1_out, A0, B0);
  and and_1 (and_1_out, A0, B0);
  or or_2 (or_2_out, A1, B1);
  and and_2 (and_2_out, A1, B1);
  or or_3 (or_3_out, A2, B2);
  and and_3 (and_3_out, A2, B2);
  or or_4 (or_4_out, A3, B3);
  and and_4 (and_4_out, A3, B3);
  and and_5 (and_5_out, or_4_out, and_3_out);
  and and_6 (and_6_out, or_4_out, or_3_out, and_2_out);
  and and_7 (and_7_out, or_4_out, or_3_out, or_2_out, and_1_out);
  and and_8 (Pg, or_4_out, or_3_out, or_2_out, or_1_out);
  or or_5 (Gg, and_4_out, and_5_out, and_6_out, and_7_out);
endmodule

module \_32位快速加法器  (
  input  C0,
  input  [31:0] A,
  input  [31:0] B,
  output ZF,
  output CF,
  output [31:0] F,
  output OF,
  output SF
);

  wire \n16位先行进位加法器_1_c16 , \n16位先行进位加法器_2_c15 , \n16位先行进位加法器_2_c16 ;

  // Probe on A
  // Probe on B
  \_16位先行进位加法器  \u_16位先行进位加法器_1  (
    .C0(C0), .A(A[15:0]), .B(B[15:0]), .S(F[15:0]), .C16(\n16位先行进位加法器_1_c16 ));  // open: C15, F_n_1
  \_16位先行进位加法器  \u_16位先行进位加法器_2  (
    .C0(\n16位先行进位加法器_1_c16 ), .A(A[31:16]), .B(B[31:16]), .S(F[31:16]), .C16(\n16位先行进位加法器_2_c16 ),
    .C15(\n16位先行进位加法器_2_c15 ), .F_n_1(SF));
  xor xor_1 (CF, C0, \n16位先行进位加法器_2_c16 );
  xor xor_2 (OF, \n16位先行进位加法器_2_c16 , \n16位先行进位加法器_2_c15 );
  // Probe on F
  nor nor_1 (ZF, F[0], F[1], F[2], F[3], F[4], F[5], F[6], F[7], F[8], F[9], F[10], F[11], F[12], F[13], F[14], F[15], F[16], F[17], F[18], F[19], F[20], F[21], F[22], F[23], F[24], F[25], F[26], F[27], F[28], F[29], F[30], F[31]);
endmodule

// XOR
module \异或门阵列  (
  input  [31:0] A,
  input  [31:0] B,
  output [31:0] Cout
);

  xor xor_1 (Cout[0], A[0], B[0]);
  xor xor_2 (Cout[1], A[1], B[1]);
  xor xor_3 (Cout[2], A[2], B[2]);
  xor xor_4 (Cout[3], A[3], B[3]);
  xor xor_5 (Cout[4], A[4], B[4]);
  xor xor_6 (Cout[5], A[5], B[5]);
  xor xor_7 (Cout[6], A[6], B[6]);
  xor xor_8 (Cout[7], A[7], B[7]);
  xor xor_9 (Cout[8], A[8], B[8]);
  xor xor_10 (Cout[9], A[9], B[9]);
  xor xor_11 (Cout[10], A[10], B[10]);
  xor xor_12 (Cout[11], A[11], B[11]);
  xor xor_13 (Cout[12], A[12], B[12]);
  xor xor_14 (Cout[13], A[13], B[13]);
  xor xor_15 (Cout[14], A[14], B[14]);
  xor xor_16 (Cout[15], A[15], B[15]);
  xor xor_17 (Cout[16], A[16], B[16]);
  xor xor_18 (Cout[17], A[17], B[17]);
  xor xor_19 (Cout[18], A[18], B[18]);
  xor xor_20 (Cout[19], A[19], B[19]);
  xor xor_21 (Cout[20], A[20], B[20]);
  xor xor_22 (Cout[21], A[21], B[21]);
  xor xor_23 (Cout[22], A[22], B[22]);
  xor xor_24 (Cout[23], A[23], B[23]);
  xor xor_25 (Cout[24], A[24], B[24]);
  xor xor_26 (Cout[25], A[25], B[25]);
  xor xor_27 (Cout[26], A[26], B[26]);
  xor xor_28 (Cout[27], A[27], B[27]);
  xor xor_29 (Cout[28], A[28], B[28]);
  xor xor_30 (Cout[29], A[29], B[29]);
  xor xor_31 (Cout[30], A[30], B[30]);
  xor xor_32 (Cout[31], A[31], B[31]);
endmodule

// OR
module \或门阵列  (
  input  [31:0] A,
  input  [31:0] B,
  output [31:0] Cout
);

  or or_1 (Cout[0], A[0], B[0]);
  or or_2 (Cout[1], A[1], B[1]);
  or or_3 (Cout[2], A[2], B[2]);
  or or_4 (Cout[3], A[3], B[3]);
  or or_5 (Cout[4], A[4], B[4]);
  or or_6 (Cout[5], A[5], B[5]);
  or or_7 (Cout[6], A[6], B[6]);
  or or_8 (Cout[7], A[7], B[7]);
  or or_9 (Cout[8], A[8], B[8]);
  or or_10 (Cout[9], A[9], B[9]);
  or or_11 (Cout[10], A[10], B[10]);
  or or_12 (Cout[11], A[11], B[11]);
  or or_13 (Cout[12], A[12], B[12]);
  or or_14 (Cout[13], A[13], B[13]);
  or or_15 (Cout[14], A[14], B[14]);
  or or_16 (Cout[15], A[15], B[15]);
  or or_17 (Cout[16], A[16], B[16]);
  or or_18 (Cout[17], A[17], B[17]);
  or or_19 (Cout[18], A[18], B[18]);
  or or_20 (Cout[19], A[19], B[19]);
  or or_21 (Cout[20], A[20], B[20]);
  or or_22 (Cout[21], A[21], B[21]);
  or or_23 (Cout[22], A[22], B[22]);
  or or_24 (Cout[23], A[23], B[23]);
  or or_25 (Cout[24], A[24], B[24]);
  or or_26 (Cout[25], A[25], B[25]);
  or or_27 (Cout[26], A[26], B[26]);
  or or_28 (Cout[27], A[27], B[27]);
  or or_29 (Cout[28], A[28], B[28]);
  or or_30 (Cout[29], A[29], B[29]);
  or or_31 (Cout[30], A[30], B[30]);
  or or_32 (Cout[31], A[31], B[31]);
endmodule

module \ALU操作控制信号生成部件  (
  input  [3:0] ALUctr,
  output SUBctr,
  output [1:0] OPctr,
  output SIGctr
);

  wire and_1_out, not_1_out, not_2_out;

  not not_1 (not_1_out, ALUctr[2]);
  not not_2 (not_2_out, ALUctr[3]);
  not not_3 (SIGctr, ALUctr[0]);
  or or_1 (SUBctr, ALUctr[1], ALUctr[3]);
  and and_1 (and_1_out, not_1_out, ALUctr[1]);
  and and_2 (OPctr[0], not_2_out, ALUctr[1]);
  or or_2 (OPctr[1], ALUctr[0], and_1_out);
endmodule
