// Logisim project RISC-V指令解析.circ as structural Verilog: 2 circuits, main circuit main
module main (
  input  [31:0] \输入指令 ,
  input  [2:0] ExtOp,
  output [6:0] out_3,
  output [2:0] out_4,
  output [4:0] out_5,
  output [4:0] out_6,
  output [4:0] out_7,
  output [31:0] out_8
);

  InstrToImm instrtoimm_1 (.Instr(\输入指令 ), .Extop(ExtOp), .imm(out_8));

  assign out_3 = \输入指令 [6:0];
  assign out_4 = \输入指令 [14:12];
  assign out_5 = \输入指令 [24:20];
  assign out_6 = \输入指令 [19:15];
  assign out_7 = \输入指令 [11:7];

  // Other names for the same wires on the sheet: imm[31:0] = out_8; op[6:0] = \输入指令 [6:0]; Rd[4:0] = \输入指令 [11:7];
  //   funct3[2:0] = \输入指令 [14:12]; Rs1[4:0] = \输入指令 [19:15]; Rs2[4:0] = \输入指令 [24:20]
endmodule

module InstrToImm (
  input  [31:0] Instr,
  input  [2:0] Extop,
  output [31:0] imm
);

  wire [11:0] bit_extender_4_out;
  wire [19:0] bit_extender_1_out, bit_extender_2_out, bit_extender_3_out;

  assign bit_extender_1_out = {{19{Instr[31]}}, Instr[31]};  // Bit_Extender bit_extender_1
  assign bit_extender_2_out = {{19{Instr[31]}}, Instr[31]};  // Bit_Extender bit_extender_2
  assign bit_extender_3_out = {{19{Instr[31]}}, Instr[31]};  // Bit_Extender bit_extender_3
  assign bit_extender_4_out = {{11{Instr[31]}}, Instr[31]};  // Bit_Extender bit_extender_4
  Multiplexer #(.select(3), .width(32), .enable("false")) multiplexer_1 (
    .in0({bit_extender_1_out, Instr[31:20]}), .in1({Instr[31:12], {12{1'b0}}}),
    .in2({bit_extender_2_out, Instr[31:25], Instr[11:7]}),
    .in3({bit_extender_3_out, Instr[7], Instr[30:25], Instr[11:8], 1'b0}),
    .in4({bit_extender_4_out, Instr[19:12], Instr[20], Instr[30:21], 1'b0}), .in5({32{1'b0}}),
    .in6({32{1'b0}}), .in7({32{1'b0}}), .out(imm), .sel(Extop));

  // Notes on the sheet:
  //   I
  //   U
  //   S
  //   B
  //   J
endmodule
