// Logisim project 控制器电路.circ as structural Verilog: 1 circuit, main circuit main
module main (
  input  funct3_0,
  input  funct3_1,
  input  funct3_2,
  input  op_0,
  input  op_1,
  input  op_2,
  input  op_3,
  input  op_4,
  input  op_5,
  input  op_6,
  output Branch,
  output Jump,
  output ALUASrc,
  output ALUBSrc_0,
  output ALUBSrc_1,
  output ALUctr_0,
  output ALUctr_1,
  output ALUctr_2,
  output ALUctr_3,
  output MemtoReg,
  output RegWr,
  output MemWr,
  output ExtOp0,
  output ExtOp1,
  output ExtOp2
);

  wire and_2_out, and_3_out, and_4_out, and_5_out, and_6_out, and_7_out, and_8_out, and_9_out, and_10_out,
       and_11_out, and_14_out, and_15_out, and_16_out, and_17_out, and_19_out, and_20_out, and_21_out,
       and_22_out, and_23_out, and_24_out, not_1_out, not_2_out, not_3_out, not_4_out, not_5_out, not_6_out,
       not_7_out, not_8_out, not_9_out, not_10_out, not_11_out, not_12_out, not_13_out, not_14_out,
       not_15_out, not_16_out, not_17_out, not_18_out, not_19_out, not_20_out, not_21_out, not_22_out,
       not_23_out, not_24_out, not_25_out, not_26_out, not_27_out, not_28_out, not_29_out, not_30_out,
       not_31_out, not_32_out, not_33_out, not_34_out, not_35_out, not_36_out;

  not not_1 (not_1_out, op_3);
  not not_2 (not_2_out, op_4);
  not not_3 (not_3_out, op_6);
  not not_4 (not_4_out, op_3);
  not not_5 (not_5_out, op_3);
  not not_6 (not_6_out, op_2);
  not not_7 (not_7_out, op_3);
  not not_8 (not_8_out, op_3);
  not not_9 (not_9_out, op_3);
  not not_10 (not_10_out, op_2);
  not not_11 (not_11_out, op_3);
  not not_12 (not_12_out, op_3);
  not not_13 (not_13_out, op_4);
  not not_14 (not_14_out, op_5);
  not not_15 (not_15_out, op_4);
  not not_16 (not_16_out, op_6);
  not not_17 (not_17_out, funct3_1);
  not not_18 (not_18_out, op_3);
  not not_19 (not_19_out, funct3_0);
  not not_20 (not_20_out, op_3);
  not not_21 (not_21_out, op_3);
  not not_22 (not_22_out, op_6);
  not not_23 (not_23_out, op_3);
  not not_24 (not_24_out, op_2);
  not not_25 (not_25_out, funct3_2);
  not not_26 (not_26_out, op_0);
  not not_27 (not_27_out, funct3_2);
  not not_28 (not_28_out, op_1);
  not not_29 (not_29_out, funct3_2);
  not not_30 (not_30_out, op_2);
  not not_31 (not_31_out, funct3_2);
  not not_32 (not_32_out, op_4);
  not not_33 (not_33_out, funct3_2);
  not not_34 (not_34_out, op_5);
  not not_35 (not_35_out, funct3_2);
  and and_1 (Branch, not_1_out, op_6);
  and and_2 (and_2_out, not_2_out, not_3_out);
  not not_36 (not_36_out, op_5);
  and and_3 (and_3_out, op_2, not_4_out);
  and and_4 (and_4_out, op_2, not_5_out);
  and and_5 (and_5_out, funct3_0, not_6_out);
  and and_6 (and_6_out, op_2, not_7_out);
  and and_7 (and_7_out, funct3_1, op_4);
  and and_8 (and_8_out, op_2, not_8_out);
  and and_9 (and_9_out, funct3_2, not_9_out);
  and and_10 (and_10_out, not_10_out, op_6);
  and and_11 (and_11_out, op_2, not_11_out);
  and and_12 (MemtoReg, not_12_out, not_13_out);
  or or_1 (RegWr, not_14_out, op_4, op_2);
  and and_13 (MemWr, not_15_out, op_5, not_16_out);
  and and_14 (and_14_out, not_17_out, not_18_out);
  and and_15 (and_15_out, not_19_out, op_2, not_20_out);
  and and_16 (and_16_out, op_0, op_1, op_2, not_21_out, op_4, op_5, not_22_out);
  and and_17 (and_17_out, funct3_2, not_23_out, op_5);
  and and_18 (ExtOp1, not_24_out, op_5);
  and and_19 (and_19_out, funct3_0, funct3_1, not_25_out, not_26_out);
  and and_20 (and_20_out, funct3_0, funct3_1, not_27_out, not_28_out);
  and and_21 (and_21_out, funct3_0, funct3_1, not_29_out, not_30_out);
  and and_22 (and_22_out, funct3_0, funct3_1, not_31_out, not_32_out);
  and and_23 (and_23_out, funct3_0, funct3_1, not_33_out, not_34_out);
  and and_24 (and_24_out, funct3_0, funct3_1, not_35_out, op_6);
  or or_2 (ALUBSrc_1, and_2_out, not_36_out, and_3_out);
  or or_3 (ALUctr_0, and_4_out, and_5_out);
  or or_4 (ALUctr_1, and_6_out, and_7_out);
  or or_5 (ALUctr_2, and_8_out, and_9_out);
  or or_6 (ALUctr_3, and_10_out, and_11_out);
  or or_7 (ExtOp0, and_14_out, and_15_out, and_16_out, and_17_out);
  or or_8 (ExtOp2, op_3, and_19_out, and_20_out, and_21_out, and_22_out, and_23_out, and_24_out);

  assign ALUASrc = op_3;
  assign ALUBSrc_0 = op_3;
  assign Jump = op_3;
endmodule
