// Logisim project 读取RAM任意地址中RISC-V指令.circ as structural Verilog: 1 circuit, main circuit main
module main (
  input  Clr,
  input  [31:0] Imm,
  input  Jump,
  input  Branch,
  input  Zero,
  output [31:0] Instr
);

  wire and_1_out, Clk_out, or_1_out;
  wire [31:0] bit_extender_1_out, multiplexer_1_out, \n32位快速加法器_1_f , PC_q;

  Clock Clk (.out(Clk_out));
  Register #(.width(32), .Select("low")) PC (.D(\n32位快速加法器_1_f ), .Q(PC_q), .clk(Clk_out), .clr(Clr));  // open: en
  assign bit_extender_1_out = {{29{1'b0}}, 3'b100};  // Bit_Extender bit_extender_1
  or or_1 (or_1_out, Jump, and_1_out);
  and and_1 (and_1_out, Branch, Zero);
  Multiplexer #(.width(32), .enable("false")) multiplexer_1 (
    .in0(bit_extender_1_out), .in1(Imm), .out(multiplexer_1_out), .sel(or_1_out));
  \_32位快速加法器  \u_32位快速加法器_1  (.C0(1'b0), .A(PC_q), .B(multiplexer_1_out), .F(\n32位快速加法器_1_f ));  // open: ZF, CF, OF, SF
  ROM #(.addrWidth(10), .dataWidth(32), .Select("low")) \u_指令存储器  (.addr(PC_q[11:2]), .data(Instr));

  // Notes on the sheet:
  //   contents of 指令存储器 (hex, n*v repeats v):
  //   111 101 1 11111 0 13435 3544
endmodule
