// Logisim project RAM存取.circ as structural Verilog: 3 circuits, main circuit main
module main (
  input  [11:0] in_1,
  input  [31:0] in_2,
  input  in_3,
  input  Clr,
  output [31:0] out_5
);

  wire clock_1_out;

  // Probe on in_2
  Clock clock_1 (.out(clock_1_out));
  RAM #(.addrWidth(12), .dataWidth(32), .bus("separate"), .Select("low")) ram_1 (
    .addr(in_1), .din(in_2), .data(out_5), .str(in_3), .clk(clock_1_out), .ld(1'b1), .clr(Clr));  // open: sel
  // Probe on out_5
endmodule

module \同步模式  (
  input  [31:0] in_1,
  input  [11:0] in_2,
  input  \读使能 ,
  input  Clr,
  output [31:0] out_5
);

  wire clock_1_out;
  wire [31:0] controlled_buffer_1_out;

  assign controlled_buffer_1_out = ~\读使能  ? in_1 : 32'bz;  // Controlled_Buffer controlled_buffer_1
  // Probe on in_1
  Clock clock_1 (.out(clock_1_out));
  RAM #(.addrWidth(12), .dataWidth(32), .Select("low")) ram_1 (
    .addr(in_2), .data(controlled_buffer_1_out), .clk(clock_1_out), .ld(\读使能 ), .clr(Clr));  // open: sel
  assign out_5 = \读使能  ? controlled_buffer_1_out : 32'bz;  // Controlled_Buffer controlled_buffer_2
  // Probe on out_5
endmodule

module \异步模式  (
  input  [31:0] in_1,
  input  [11:0] in_2,
  input  \读使能 ,
  input  Clr,
  output [31:0] out_5
);

  wire [31:0] controlled_buffer_1_out;

  assign controlled_buffer_1_out = ~\读使能  ? in_1 : 32'bz;  // Controlled_Buffer controlled_buffer_1
  // Probe on in_1
  RAM #(.addrWidth(12), .dataWidth(32), .bus("asynch"), .Select("low")) ram_1 (
    .addr(in_2), .data(controlled_buffer_1_out), .ld(\读使能 ), .clr(Clr));  // open: sel
  assign out_5 = \读使能  ? controlled_buffer_1_out : 32'bz;  // Controlled_Buffer controlled_buffer_2
  // Probe on out_5
endmodule
